# Fritzing sketch lec01-02 (saved by Fritzing 0.9.3b)
circuit board: 8.46667cm x 5.64444cm
breadboards: 2

parts:
  부품1 = Arduino Mega 2560 (Rev3)
  부품2 = 8*8 LED Matrix - RED [part_number=SZH-EK062]

nets:
  N1: 부품1.D21/SCL, 부품2.Pin_16
  N2: 부품1.D20/SDA, 부품2.Pin_15
  N3: 부품1.D19/RX1, 부품2.Pin_14
  N4: 부품1.D17_PWM/RX2, 부품1.D16_PWM/TX2, 부품1.D0_RX0, 부품1.D1_TX0, 부품2.Pin_1, 부품2.Pin_2, 부품2.Pin_11, 부품2.Pin_12
  N5: 부품1.D15/RX3, 부품1.D2_PWM, 부품2.Pin_3, 부품2.Pin_10
  N6: 부품1.D14/TX3, 부품1.D3_PWM, 부품2.Pin_4, 부품2.Pin_9
  N7: 부품1.D4_PWM, 부품2.Pin_5
  N8: 부품1.D5_PWM, 부품1.D6_PWM, 부품2.Pin_6, 부품2.Pin_7
  N9: 부품1.D7_PWM, 부품2.Pin_8

custom parts:
  8*8 LED Matrix - RED: Description: This is a large sized RGB LED Matrix with a backpack that has been designed to take SPI serial input and display any graphics you pass it. All the refreshing and communication control is taken care of by the backpack. It's even reprogrammable! 7 software selectable colors are available! Unit comes with a Red/Green/Blue LED Matrix assembled with a RGB Matrix Backpack Controller.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
